// Logisim project Trabalho ULA.circ as structural Verilog: 1 circuit, main circuit main
module main (
  input  [2:0] S,
  input  [7:0] A,
  input  [7:0] B,
  output [7:0] Y
);

  wire [7:0] adder_1_out, and_1_out, demultiplexer_1_out0, demultiplexer_1_out1, demultiplexer_1_out2,
       demultiplexer_1_out4, demultiplexer_1_out5, demultiplexer_1_out6, demultiplexer_2_out0,
       demultiplexer_2_out1, demultiplexer_2_out3, demultiplexer_2_out4, demultiplexer_2_out5,
       demultiplexer_2_out6, not_1_out, not_2_out, or_1_out, subtractor_1_out, xor_1_out;

  Demultiplexer #(.select(3), .width(8), .enable("false")) demultiplexer_1 (
    .out0(demultiplexer_1_out0), .out1(demultiplexer_1_out1), .out2(demultiplexer_1_out2),
    .out4(demultiplexer_1_out4), .out5(demultiplexer_1_out5), .out6(demultiplexer_1_out6), .in(A), .sel(S));  // open: out3, out7
  Demultiplexer #(.select(3), .width(8), .enable("false")) demultiplexer_2 (
    .out0(demultiplexer_2_out0), .out1(demultiplexer_2_out1), .out3(demultiplexer_2_out3),
    .out4(demultiplexer_2_out4), .out5(demultiplexer_2_out5), .out6(demultiplexer_2_out6), .in(B), .sel(S));  // open: out2, out7
  Adder adder_1 (.a(demultiplexer_1_out0), .b(demultiplexer_2_out0), .out(adder_1_out));  // open: cin, cout
  Subtractor subtractor_1 (
    .a(demultiplexer_1_out1), .b(demultiplexer_2_out1), .out(subtractor_1_out));  // open: bin, bout
  assign not_1_out = ~demultiplexer_1_out2;  // NOT_Gate not_1, 8 bits wide
  assign not_2_out = ~demultiplexer_2_out3;  // NOT_Gate not_2, 8 bits wide
  assign and_1_out = demultiplexer_1_out4 & demultiplexer_2_out4;  // AND_Gate and_1, 8 bits wide
  assign or_1_out = demultiplexer_1_out5 | demultiplexer_2_out5;  // OR_Gate or_1, 8 bits wide
  assign xor_1_out = demultiplexer_1_out6 ^ demultiplexer_2_out6;  // XOR_Gate xor_1, 8 bits wide
  Multiplexer #(.select(3), .width(8), .enable("false")) multiplexer_1 (
    .in0(adder_1_out), .in1(subtractor_1_out), .in2(not_1_out), .in3(not_2_out), .in4(and_1_out),
    .in5(or_1_out), .in6(xor_1_out), .out(Y), .sel(S));  // open: in7
endmodule
