// Logisim project exercicio 1.circ as structural Verilog: 1 circuit, main circuit main
module main (
  input  A,
  input  A_2,
  input  A_3,
  input  B,
  input  B_2,
  input  A_4,
  input  A_5,
  input  B_3,
  input  B_4,
  input  A_6,
  input  A_7,
  input  B_5,
  input  B_6,
  output out_14,
  output out_15,
  output out_16,
  output out_17,
  output out_18,
  output out_19,
  output out_20
);

  not not_1 (out_14, A);
  and and_1 (out_16, A_3, B_2);
  or or_1 (out_18, A_5, B_4);
  nand nand_1 (out_20, A_7, B_6);
  nor nor_1 (out_15, A_2, B);
  xor xor_1 (out_17, A_4, B_3);
  xnor xnor_1 (out_19, A_6, B_5);

  // Notes on the sheet:
  //   NOT
  //   AND
  //   OR
  //   NAND
  //   NOR
  //   XOR
  //   XNOR
endmodule
